# Fritzing sketch Reciever (saved by Fritzing 0.9.3b)
circuit board: 8.46667cm x 5.64444cm

parts:
  Part1 = Arduino Uno (Rev3)
  S1 = H-Bridge with L298N
  VCC1 = Battery
  VCC2 = Battery
  M1 = DC Motor
  M2 = DC Motor
  Part2 = NRF24L01+ Breakout Board
  BAT1 = BC9VPC [package=bc9vpc]
  U1 = SWITCH_SPDT [package=kps-1290]

nets:
  N1: Part1.D9_PWM, Part2.CE
  N2: Part1.D10_PWM/SS, Part2.CS
  N3: Part1.D11_PWM/MOSI, Part2.MOSI
  N4: Part1.D12/MISO, Part2.MISO
  N5: Part1.D13/SCK, Part2.SCK
  GND: Part1.GND, S1.GND, VCC2.-, Part2.GND, BAT1.V-
  N6: Part1.D2, Part2.IRQ
  N7: Part1.D4, S1.IN4
  N8: Part1.D5_PWM, S1.IN3
  N9: Part1.D6_PWM, S1.IN2
  N10: Part1.D7, S1.IN1
  3V3: Part1.3V3, Part2.VCC
  N11: Part1.VIN, U1.P
  N12: S1.12V, VCC1.+
  N13: S1.M1-01, M1.pin_2
  N14: S1.M1-02, M1.pin_1
  N15: S1.M2-01, M2.pin_2
  N16: S1.M2-02, M2.pin_1

custom parts:
  H-Bridge with L298N: h-bridge
