# Fritzing sketch Transmitter (saved by Fritzing 0.9.3b)
breadboards: 1

parts:
  Part1 = Arduino Uno (Rev3)
  Part2 = NRF24L01+ Breakout Board
  U1 = Wiichuck Adapter

nets:
  N1: Part1.A4/SDA, U1.SCL
  N2: Part1.A5/SCL, U1.SDA
  N3: Part1.D9_PWM, Part2.CE
  N4: Part1.D10_PWM/SS, Part2.CS
  N5: Part1.D11_PWM/MOSI, Part2.MOSI
  N6: Part1.D12/MISO, Part2.MISO
  N7: Part1.D13/SCK, Part2.SCK
  3V3: Part1.3V3, Part2.VCC
  N8: Part1.5V, U1.+
  GND: Part1.GND, Part2.GND, U1.-

custom parts:
  Wiichuck Adapter: SCP1000 Barometric Pressure sensor. Can sense air pressure and temperature. SPI interface.
